// Logisim project main.circ as structural Verilog: 8 circuits, main circuit СДНФ
module \СДНФ  (
  input  x3,
  input  x2,
  input  x1,
  input  x0,
  output out_5
);

  wire and_1_out, and_2_out, and_3_out, and_4_out, and_5_out, and_6_out, and_7_out, and_8_out, not_1_out,
       not_2_out, not_3_out, not_4_out, not_5_out, not_6_out, not_7_out, not_8_out, not_9_out, not_10_out,
       not_11_out;

  not not_1 (not_1_out, x3);
  not not_2 (not_2_out, x2);
  not not_3 (not_3_out, x0);
  not not_4 (not_4_out, x3);
  not not_5 (not_5_out, x0);
  not not_6 (not_6_out, x3);
  not not_7 (not_7_out, x2);
  not not_8 (not_8_out, x1);
  not not_9 (not_9_out, x2);
  not not_10 (not_10_out, x1);
  not not_11 (not_11_out, x0);
  and and_1 (and_1_out, not_1_out, not_2_out, x1, not_3_out);
  and and_2 (and_2_out, not_4_out, x2, x1, not_5_out);
  and and_3 (and_3_out, not_6_out, x2, x1, x0);
  and and_4 (and_4_out, x3, not_7_out, not_8_out, x0);
  and and_5 (and_5_out, x3, not_9_out, x1, x0);
  and and_6 (and_6_out, x3, x2, not_10_out, x0);
  and and_7 (and_7_out, x3, x2, x1, not_11_out);
  and and_8 (and_8_out, x3, x2, x1, x0);
  or or_1 (out_5, and_1_out, and_2_out, and_3_out, and_4_out, and_5_out, and_6_out, and_7_out, and_8_out);
endmodule

module \СКНФ  (
  input  x3,
  input  x2,
  input  x1,
  input  x0,
  output out_5
);

  wire not_1_out, not_2_out, not_3_out, not_4_out, not_5_out, not_6_out, not_7_out, not_8_out, not_9_out,
       not_10_out, not_11_out, or_1_out, or_2_out, or_3_out, or_4_out, or_5_out, or_6_out, or_7_out, or_8_out;

  or or_1 (or_1_out, x3, x2, x1, x0);
  or or_2 (or_2_out, x3, x2, x1, not_1_out);
  not not_1 (not_1_out, x0);
  or or_3 (or_3_out, x3, x2, not_2_out, not_3_out);
  not not_2 (not_2_out, x1);
  not not_3 (not_3_out, x0);
  not not_4 (not_4_out, x2);
  or or_4 (or_4_out, x3, not_4_out, x1, x0);
  not not_5 (not_5_out, x2);
  or or_5 (or_5_out, x3, not_5_out, x1, not_6_out);
  not not_6 (not_6_out, x0);
  not not_7 (not_7_out, x3);
  or or_6 (or_6_out, not_7_out, x2, x1, x0);
  not not_8 (not_8_out, x3);
  or or_7 (or_7_out, not_8_out, x2, not_9_out, x0);
  not not_9 (not_9_out, x1);
  not not_10 (not_10_out, x3);
  not not_11 (not_11_out, x2);
  or or_8 (or_8_out, not_10_out, not_11_out, x1, x0);
  and and_1 (out_5, or_1_out, or_2_out, or_3_out, or_4_out, or_5_out, or_6_out, or_7_out, or_8_out);
endmodule

module \МДНФ  (
  input  x3,
  input  x2,
  input  x1,
  input  x0,
  output x
);

  wire and_1_out, and_2_out, and_3_out, and_4_out, not_1_out, not_2_out, or_1_out;

  not not_1 (not_1_out, x3);
  and and_1 (and_1_out, not_1_out, x1);
  and and_2 (and_2_out, and_1_out, not_2_out);
  not not_2 (not_2_out, x0);
  and and_3 (and_3_out, x2, x1);
  or or_1 (or_1_out, and_2_out, and_3_out);
  and and_4 (and_4_out, x3, x0);
  or or_2 (x, or_1_out, and_4_out);
endmodule

module \МКНФ  (
  input  x3,
  input  x2,
  input  x1,
  input  x0,
  output x
);

  wire and_1_out, and_2_out, not_1_out, not_2_out, or_1_out, or_2_out, or_3_out, or_4_out, or_5_out, or_6_out;

  or or_1 (or_1_out, x3, x2);
  not not_1 (not_1_out, x0);
  not not_2 (not_2_out, x3);
  or or_2 (or_2_out, not_2_out, x2);
  or or_3 (or_3_out, x3, x1);
  or or_4 (or_4_out, x1, x0);
  or or_5 (or_5_out, or_1_out, not_1_out);
  or or_6 (or_6_out, or_2_out, x0);
  and and_1 (and_1_out, or_3_out, or_4_out);
  and and_2 (and_2_out, or_5_out, or_6_out);
  and and_3 (x, and_1_out, and_2_out);
endmodule

module \Генератор___СДНФ  (
);

  wire and_1_out, and_2_out, and_3_out, and_4_out, and_5_out, and_6_out, and_7_out, and_8_out, not_1_out,
       not_2_out, not_3_out, not_4_out, not_5_out, not_6_out, not_7_out, not_8_out, not_9_out, not_10_out,
       not_11_out, or_1_out, x0_out, x1_out, x2_out, x3_out;

  Clock #(.highDuration(8), .lowDuration(8)) x3 (.out(x3_out));
  Clock #(.highDuration(4), .lowDuration(4)) x2 (.out(x2_out));
  Clock #(.highDuration(2), .lowDuration(2)) x1 (.out(x1_out));
  Clock x0 (.out(x0_out));
  not not_1 (not_1_out, x3_out);
  not not_2 (not_2_out, x2_out);
  not not_3 (not_3_out, x0_out);
  not not_4 (not_4_out, x3_out);
  not not_5 (not_5_out, x0_out);
  not not_6 (not_6_out, x3_out);
  not not_7 (not_7_out, x2_out);
  not not_8 (not_8_out, x1_out);
  not not_9 (not_9_out, x2_out);
  not not_10 (not_10_out, x1_out);
  not not_11 (not_11_out, x0_out);
  and and_1 (and_1_out, not_1_out, not_2_out, x1_out, not_3_out);
  and and_2 (and_2_out, not_4_out, x2_out, x1_out, not_5_out);
  and and_3 (and_3_out, not_6_out, x2_out, x1_out, x0_out);
  and and_4 (and_4_out, x3_out, not_7_out, not_8_out, x0_out);
  and and_5 (and_5_out, x3_out, not_9_out, x1_out, x0_out);
  and and_6 (and_6_out, x3_out, x2_out, not_10_out, x0_out);
  and and_7 (and_7_out, x3_out, x2_out, x1_out, not_11_out);
  and and_8 (and_8_out, x3_out, x2_out, x1_out, x0_out);
  or or_1 (or_1_out, and_1_out, and_2_out, and_3_out, and_4_out, and_5_out, and_6_out, and_7_out, and_8_out);
  LED led_1 (.in(or_1_out));
endmodule

module \Генератор___СКНФ  (
);

  wire and_1_out, not_1_out, not_2_out, not_3_out, not_4_out, not_5_out, not_6_out, not_7_out, not_8_out,
       not_9_out, not_10_out, not_11_out, or_1_out, or_2_out, or_3_out, or_4_out, or_5_out, or_6_out,
       or_7_out, or_8_out, x0_out, x1_out, x2_out, x3_out;

  Clock #(.highDuration(8), .lowDuration(8)) x3 (.out(x3_out));
  Clock #(.highDuration(4), .lowDuration(4)) x2 (.out(x2_out));
  Clock #(.highDuration(2), .lowDuration(2)) x1 (.out(x1_out));
  Clock x0 (.out(x0_out));
  or or_1 (or_1_out, x3_out, x2_out, x1_out, x0_out);
  or or_2 (or_2_out, x3_out, x2_out, x1_out, not_1_out);
  not not_1 (not_1_out, x0_out);
  or or_3 (or_3_out, x3_out, x2_out, not_2_out, not_3_out);
  not not_2 (not_2_out, x1_out);
  not not_3 (not_3_out, x0_out);
  not not_4 (not_4_out, x2_out);
  or or_4 (or_4_out, x3_out, not_4_out, x1_out, x0_out);
  not not_5 (not_5_out, x2_out);
  or or_5 (or_5_out, x3_out, not_5_out, x1_out, not_6_out);
  not not_6 (not_6_out, x0_out);
  not not_7 (not_7_out, x3_out);
  or or_6 (or_6_out, not_7_out, x2_out, x1_out, x0_out);
  not not_8 (not_8_out, x3_out);
  or or_7 (or_7_out, not_8_out, x2_out, not_9_out, x0_out);
  not not_9 (not_9_out, x1_out);
  not not_10 (not_10_out, x3_out);
  not not_11 (not_11_out, x2_out);
  or or_8 (or_8_out, not_10_out, not_11_out, x1_out, x0_out);
  and and_1 (and_1_out, or_1_out, or_2_out, or_3_out, or_4_out, or_5_out, or_6_out, or_7_out, or_8_out);
  LED led_1 (.in(and_1_out));
endmodule

module \Генератор___МДНФ  (
);

  wire and_1_out, and_2_out, and_3_out, and_4_out, not_1_out, not_2_out, or_1_out, or_2_out, x0_out, x1_out,
       x2_out, x3_out;

  Clock #(.highDuration(8), .lowDuration(8)) x3 (.out(x3_out));
  Clock #(.highDuration(4), .lowDuration(4)) x2 (.out(x2_out));
  Clock #(.highDuration(2), .lowDuration(2)) x1 (.out(x1_out));
  Clock x0 (.out(x0_out));
  not not_1 (not_1_out, x3_out);
  and and_1 (and_1_out, not_1_out, x1_out);
  and and_2 (and_2_out, and_1_out, not_2_out);
  not not_2 (not_2_out, x0_out);
  and and_3 (and_3_out, x2_out, x1_out);
  or or_1 (or_1_out, and_2_out, and_3_out);
  and and_4 (and_4_out, x3_out, x0_out);
  LED led_1 (.in(or_2_out));
  or or_2 (or_2_out, or_1_out, and_4_out);
endmodule

module \Генератор_МКНФ  (
);

  wire and_1_out, and_2_out, and_3_out, not_1_out, not_2_out, or_1_out, or_2_out, or_3_out, or_4_out,
       or_5_out, or_6_out, x0_out, x1_out, x2_out, x3_out;

  Clock #(.highDuration(8), .lowDuration(8)) x3 (.out(x3_out));
  Clock #(.highDuration(4), .lowDuration(4)) x2 (.out(x2_out));
  Clock #(.highDuration(2), .lowDuration(2)) x1 (.out(x1_out));
  Clock x0 (.out(x0_out));
  not not_1 (not_1_out, x3_out);
  or or_1 (or_1_out, x3_out, x2_out);
  not not_2 (not_2_out, x0_out);
  or or_2 (or_2_out, not_1_out, x2_out);
  or or_3 (or_3_out, x3_out, x1_out);
  or or_4 (or_4_out, x1_out, x0_out);
  or or_5 (or_5_out, or_1_out, not_2_out);
  or or_6 (or_6_out, or_2_out, x0_out);
  and and_1 (and_1_out, or_3_out, or_4_out);
  and and_2 (and_2_out, or_5_out, or_6_out);
  and and_3 (and_3_out, and_1_out, and_2_out);
  LED led_1 (.in(and_3_out));
endmodule
